// Logisim project C4 Quiz logisim.circ as structural Verilog: 1 circuit, main circuit main
module main (
  input  in_1,
  input  in_2,
  input  in_3,
  input  in_4,
  input  in_5,
  output out_6,
  output out_7,
  output out_8
);

  wire and_1_out, and_3_out, and_4_out, and_5_out, and_6_out, clock_1_out, not_1_out, not_3_out;

  Clock clock_1 (.out(clock_1_out));
  not not_1 (not_1_out, in_3);
  and and_1 (and_1_out, not_1_out, out_7);
  and and_2 (out_6, in_1, out_6);
  or or_1 (out_7, in_2, and_1_out);
  and and_3 (and_3_out, in_4, clock_1_out);
  and and_4 (and_4_out, clock_1_out, in_5);
  and and_5 (and_5_out, and_3_out, and_3_out, not_3_out);
  and and_6 (and_6_out, out_8, and_4_out);
  not not_2 (out_8, and_5_out);
  not not_3 (not_3_out, and_6_out);
endmodule
