// Logisim project half adder.circ as structural Verilog: 2 circuits, main circuit Half adder
module Half_adder (
  input  in_1,
  input  in_2,
  output out_3,
  output out_4
);

  wire and_1_out, and_2_out, not_1_out, not_2_out;

  not not_1 (not_1_out, in_2);
  not not_2 (not_2_out, in_1);
  and and_1 (and_1_out, in_1, not_1_out);
  and and_2 (and_2_out, not_2_out, in_2);
  and and_3 (out_4, in_2, in_1);
  or or_1 (out_3, and_1_out, and_2_out);
endmodule

module Full_adder (
  input  in_1,
  input  in_2,
  input  in_3,
  input  in_4,
  input  in_5,
  input  in_6,
  input  in_7,
  input  in_8,
  input  in_9,
  output out_10,
  output out_11,
  output out_12,
  output out_13,
  output out_14
);

  wire half_adder_1_out_4, half_adder_2_out_4, half_adder_3_out_4;

  Half_adder half_adder_1 (.in_1(in_1), .in_2(in_2), .out_3(out_10), .out_4(half_adder_1_out_4));
  Half_adder half_adder_2 (.in_1(in_4), .in_2(in_5), .out_3(out_11), .out_4(half_adder_2_out_4));
  Half_adder half_adder_3 (.in_1(in_6), .in_2(in_7), .out_3(out_12), .out_4(half_adder_3_out_4));
  Half_adder half_adder_4 (.in_1(in_8), .in_2(in_9), .out_3(out_13), .out_4(out_14));
endmodule
